// Logisim project SPC32.circ as structural Verilog: 11 circuits, main circuit main
module main (
);

  wire programcounter_1_readmem;
  wire [2:0] opcodedecoder_1_imm_type;
  wire [6:0] instrdecoder_1_opcode;
  wire [31:0] memory_1_out_data, programcounter_1_outputaddress;

  ProgramCounter programcounter_1 (
    .OutputAddress(programcounter_1_outputaddress), .ReadMem(programcounter_1_readmem));  // open: InputAddress, FETCH, Load
  RegisterFile registerfile_1 ();  // open: DATA, RS1, RS2, RD, WRITE, OUT1, OUT2
  Memory memory_1 (
    .ADRESS(programcounter_1_outputaddress), .READ(programcounter_1_readmem), .OUT_DATA(memory_1_out_data));  // open: WRITE, IN_DATA
  InstrDecoder instrdecoder_1 (
    .INSTR(memory_1_out_data), .IMM_TYPE(opcodedecoder_1_imm_type), .OPCODE(instrdecoder_1_opcode));  // open: RD, funct3, RS1, RS2, funct7, IMMEDIATE
  OpcodeDecoder opcodedecoder_1 (.OPCODE(instrdecoder_1_opcode), .IMM_TYPE(opcodedecoder_1_imm_type));  // open: ERROR
endmodule

module Conditions (
  input  ACTIVE,
  input  [7:0] REG0,
  output JMP
);

  wire comparator_1_eq;

  Comparator comparator_1 (.a(REG0), .b({8{1'b0}}), .eq(comparator_1_eq));  // open: gt, lt
  assign JMP = ACTIVE ? comparator_1_eq : 1'bz;  // Controlled_Buffer controlled_buffer_1
endmodule

module ALU8 (
  input  [7:0] ARG1,
  input  [7:0] ARG2,
  input  [1:0] OPCODE,
  input  [3:0] Const,
  input  ACTIVE,
  output [7:0] RESULT
);

  wire [7:0] adder_1_out, bit_extender_1_out, multiplexer_1_out, nand_1_out, subtractor_1_out, xor_1_out;

  assign nand_1_out = ~(ARG1 & ARG2);  // NAND_Gate nand_1, 8 bits wide
  assign xor_1_out = ARG1 ^ ARG2;  // XOR_Gate xor_1, 8 bits wide
  Subtractor subtractor_1 (.a(ARG1), .b(ARG2), .out(subtractor_1_out));  // open: bin, bout
  Adder adder_1 (.a(ARG1), .b(ARG2), .out(adder_1_out));  // open: cin, cout
  Multiplexer #(.enable("true"), .select(2), .width(8)) multiplexer_1 (
    .in0(adder_1_out), .in1(subtractor_1_out), .in2(xor_1_out), .in3(nand_1_out), .out(multiplexer_1_out),
    .sel(OPCODE), .en(ACTIVE));
  Adder adder_2 (.a(multiplexer_1_out), .b(bit_extender_1_out), .out(RESULT));  // open: cin, cout
  assign bit_extender_1_out = {{4{1'b0}}, Const};  // Bit_Extender bit_extender_1
  Conditions conditions_1 ();  // open: ACTIVE, REG0, JMP
endmodule

module RegisterBank (
  input  [2:0] WriteReg,
  input  WRITE,
  input  READ,
  input  [7:0] InputData,
  input  [2:0] ReadReg,
  output [7:0] OutputData,
  output [7:0] ARG0,
  output [7:0] ARG1,
  output [7:0] ARG2,
  output [7:0] RamAdress
);

  wire CLOCK_GEN_out, decoder_1_out0, decoder_1_out1, decoder_1_out2, decoder_1_out3, decoder_1_out4,
       decoder_1_out5, decoder_1_out6, decoder_1_out7;
  wire [7:0] REG3_q, REG4_q, REG5_q, REG6_q;

  Clock CLOCK_GEN (.out(CLOCK_GEN_out));
  Decoder #(.select(3)) decoder_1 (
    .out0(decoder_1_out0), .out1(decoder_1_out1), .out2(decoder_1_out2), .out3(decoder_1_out3),
    .out4(decoder_1_out4), .out5(decoder_1_out5), .out6(decoder_1_out6), .out7(decoder_1_out7),
    .sel(WriteReg), .en(WRITE));
  Register REG0 (.D(InputData), .en(decoder_1_out0), .clk(CLOCK_GEN_out), .Q(ARG0));  // open: clr
  Register REG1 (.D(InputData), .en(decoder_1_out1), .clk(CLOCK_GEN_out), .Q(ARG1));  // open: clr
  Register REG2 (.D(InputData), .en(decoder_1_out2), .clk(CLOCK_GEN_out), .Q(ARG2));  // open: clr
  Register REG3 (.D(InputData), .en(decoder_1_out3), .clk(CLOCK_GEN_out), .Q(REG3_q));  // open: clr
  Register REG4 (.D(InputData), .en(decoder_1_out4), .clk(CLOCK_GEN_out), .Q(REG4_q));  // open: clr
  Register REG5 (.D(InputData), .en(decoder_1_out5), .clk(CLOCK_GEN_out), .Q(REG5_q));  // open: clr
  Register REG6 (.D(InputData), .en(decoder_1_out6), .clk(CLOCK_GEN_out), .Q(REG6_q));  // open: clr
  Register REG7 (.D(InputData), .en(decoder_1_out7), .clk(CLOCK_GEN_out), .Q(RamAdress));  // open: clr
  Multiplexer #(.enable("true"), .select(3), .width(8)) multiplexer_1 (
    .in0(ARG0), .in1(ARG1), .in2(ARG2), .in3(REG3_q), .in4(REG4_q), .in5(REG5_q), .in6(REG6_q),
    .in7(RamAdress), .out(OutputData), .sel(ReadReg), .en(READ));

  // Notes on the sheet:
  //   READ: pull=down
endmodule

module ProgramCounter (
  input  [31:0] InputAddress,
  input  FETCH,
  input  Load,
  output [31:0] OutputAddress,
  output ReadMem
);

  wire clock_1_out;
  wire [31:0] adder_1_out, multiplexer_1_out, register_1_q;

  Clock clock_1 (.out(clock_1_out));
  Multiplexer #(.width(32)) multiplexer_1 (.in0(adder_1_out), .in1(InputAddress), .out(multiplexer_1_out), .sel(Load));
  Register #(.width(32)) register_1 (
    .D(multiplexer_1_out), .en(FETCH), .clk(clock_1_out), .Q(register_1_q));  // open: clr
  assign OutputAddress = FETCH ? register_1_q : 32'bz;  // Controlled_Buffer controlled_buffer_1
  Adder #(.width(32)) adder_1 (.a(32'h4), .b(register_1_q), .out(adder_1_out));  // open: cin, cout

  assign ReadMem = FETCH;

  // Notes on the sheet:
  //   Load: pull=down
endmodule

module InstrDecoder (
  input  [31:0] INSTR,
  input  [2:0] IMM_TYPE,
  output [6:0] OPCODE,
  output [4:0] RD,
  output [2:0] funct3,
  output [4:0] RS1,
  output [4:0] RS2,
  output [6:0] funct7,
  output [31:0] IMMEDIATE
);

  wire [31:0] bit_extender_1_out, bit_extender_2_out, bit_extender_3_out;

  assign bit_extender_1_out = {{20{1'b0}}, INSTR[31:20]};  // Bit_Extender bit_extender_1
  assign bit_extender_2_out = {{20{1'b0}}, {INSTR[31:25], INSTR[11:7]}};  // Bit_Extender bit_extender_2
  assign bit_extender_3_out = {{19{1'b0}}, {INSTR[31], INSTR[7], INSTR[30:25], INSTR[11:8], 1'b0}};  // Bit_Extender bit_extender_3
  Multiplexer #(.select(3), .width(32)) multiplexer_1 (
    .in1(bit_extender_1_out), .in2(bit_extender_2_out), .in3(bit_extender_3_out),
    .in4({INSTR[31:12], {12{1'b0}}}),
    .in5({{11{1'b0}}, INSTR[31], INSTR[19:12], INSTR[20], INSTR[30:21], 1'b0}), .out(IMMEDIATE),
    .sel(IMM_TYPE));  // open: in0, in6, in7

  assign funct3 = INSTR[14:12];
  assign funct7 = INSTR[31:25];
  assign OPCODE = INSTR[6:0];
  assign RD = INSTR[11:7];
  assign RS1 = INSTR[19:15];
  assign RS2 = INSTR[24:20];

  // Notes on the sheet:
  //   I-TYPE IMMEDIATE
  //   S-TYPE IMMEDIATE
  //   B-TYPE IMMEDIATE
  //   U-TYPE IMMEDIATE
  //   J-TYPE IMMEDIATE
endmodule

module Memory (
  input  [31:0] ADRESS,
  input  WRITE,
  input  READ,
  input  [31:0] IN_DATA,
  output [31:0] OUT_DATA
);

  wire clock_1_out;

  RAM #(.addrWidth(16), .dataWidth(32), .\type ("nonvolatile")) ram_1 (
    .addr(ADRESS[17:2]), .we(WRITE), .oe(READ), .clk(clock_1_out), .din(IN_DATA), .dout(OUT_DATA));
  Clock clock_1 (.out(clock_1_out));

  // Notes on the sheet:
  //   WRITE: pull=down
  //   READ: pull=down
endmodule

module OpcodeDecoder (
  input  [6:0] OPCODE,
  output ERROR,
  output [2:0] IMM_TYPE
);

  wire decoder_1_out0, decoder_1_out1, decoder_1_out4, decoder_1_out8, decoder_1_out13, decoder_1_out24,
       decoder_1_out27, decoder_1_out28, not_1_out, or_1_out, or_2_out;

  not not_1 (not_1_out, ERROR);
  nand nand_1 (ERROR, OPCODE[0], OPCODE[1]);
  Decoder #(.select(5)) decoder_1 (
    .out0(decoder_1_out0), .out1(decoder_1_out1), .out4(decoder_1_out4), .out8(decoder_1_out8),
    .out13(decoder_1_out13), .out24(decoder_1_out24), .out27(decoder_1_out27), .out28(decoder_1_out28),
    .sel(OPCODE[6:2]), .en(not_1_out));  // open: out2, out3, out5, out6, out7, out9, out10, out11, out12, out14, out15, out16, out17, out18, out19, out20, out21, out22, out23, out25, out26, out29, out30, out31
  or or_1 (or_1_out, decoder_1_out4, decoder_1_out28, decoder_1_out0);
  assign IMM_TYPE = or_1_out ? 3'b001 : 3'bz;  // Controlled_Buffer controlled_buffer_1
  assign IMM_TYPE = decoder_1_out8 ? 3'b010 : 3'bz;  // Controlled_Buffer controlled_buffer_2
  or or_2 (or_2_out, decoder_1_out13, decoder_1_out1);
  assign IMM_TYPE = decoder_1_out24 ? 3'b011 : 3'bz;  // Controlled_Buffer controlled_buffer_3
  assign IMM_TYPE = or_2_out ? 3'b100 : 3'bz;  // Controlled_Buffer controlled_buffer_4
  assign IMM_TYPE = decoder_1_out27 ? 3'b101 : 3'bz;  // Controlled_Buffer controlled_buffer_5
endmodule

module RegisterFile (
  input  [31:0] DATA,
  input  [4:0] RS1,
  input  [4:0] RS2,
  input  [4:0] RD,
  input  WRITE,
  output [31:0] OUT1,
  output [31:0] OUT2
);

  wire decoder_1_out0, decoder_1_out1, decoder_1_out2, decoder_1_out3;
  wire [31:0] registerbank8_1_out1, registerbank8_1_out2, registerbank8_2_out1, registerbank8_2_out2,
       registerbank8_3_out1, registerbank8_3_out2, registerbank8zero_1_out1, registerbank8zero_1_out2;

  Decoder #(.select(2)) decoder_1 (
    .out0(decoder_1_out0), .out1(decoder_1_out1), .out2(decoder_1_out2), .out3(decoder_1_out3),
    .sel(RD[4:3]), .en(WRITE));
  RegisterBank8Zero registerbank8zero_1 (
    .RS1(RS1[2:0]), .RS2(RS2[2:0]), .DATA(DATA), .WRITE(decoder_1_out0), .RD(RD[2:0]),
    .OUT1(registerbank8zero_1_out1), .OUT2(registerbank8zero_1_out2));
  RegisterBank8 registerbank8_1 (
    .RS1(RS1[2:0]), .RS2(RS2[2:0]), .DATA(DATA), .WRITE(decoder_1_out1), .RD(RD[2:0]),
    .OUT1(registerbank8_1_out1), .OUT2(registerbank8_1_out2));
  RegisterBank8 registerbank8_2 (
    .RS1(RS1[2:0]), .RS2(RS2[2:0]), .DATA(DATA), .WRITE(decoder_1_out2), .RD(RD[2:0]),
    .OUT1(registerbank8_2_out1), .OUT2(registerbank8_2_out2));
  RegisterBank8 registerbank8_3 (
    .RS1(RS1[2:0]), .RS2(RS2[2:0]), .DATA(DATA), .WRITE(decoder_1_out3), .RD(RD[2:0]),
    .OUT1(registerbank8_3_out1), .OUT2(registerbank8_3_out2));
  Multiplexer #(.select(2), .width(32)) multiplexer_1 (
    .in0(registerbank8_3_out1), .in1(registerbank8_2_out1), .in2(registerbank8_1_out1),
    .in3(registerbank8zero_1_out1), .out(OUT1), .sel(RS1[4:3]));
  Multiplexer #(.select(2), .width(32)) multiplexer_2 (
    .in0(registerbank8_3_out2), .in1(registerbank8_2_out2), .in2(registerbank8_1_out2),
    .in3(registerbank8zero_1_out2), .out(OUT2), .sel(RS2[4:3]));
endmodule

module RegisterBank8 (
  input  [2:0] RS1,
  input  [2:0] RS2,
  input  [31:0] DATA,
  input  WRITE,
  input  [2:0] RD,
  output [31:0] OUT1,
  output [31:0] OUT2
);

  wire clock_1_out, decoder_1_out0, decoder_1_out1, decoder_1_out2, decoder_1_out3, decoder_1_out4,
       decoder_1_out5, decoder_1_out6, decoder_1_out7;
  wire [31:0] register_1_q, register_2_q, register_3_q, register_4_q, register_5_q, register_6_q,
       register_7_q, register_8_q;

  Clock clock_1 (.out(clock_1_out));
  Decoder #(.select(3)) decoder_1 (
    .out0(decoder_1_out0), .out1(decoder_1_out1), .out2(decoder_1_out2), .out3(decoder_1_out3),
    .out4(decoder_1_out4), .out5(decoder_1_out5), .out6(decoder_1_out6), .out7(decoder_1_out7), .sel(RD),
    .en(WRITE));
  Register #(.width(32)) register_1 (.D(DATA), .en(decoder_1_out0), .clk(clock_1_out), .Q(register_1_q));  // open: clr
  Register #(.width(32)) register_2 (.D(DATA), .en(decoder_1_out1), .clk(clock_1_out), .Q(register_2_q));  // open: clr
  Register #(.width(32)) register_3 (.D(DATA), .en(decoder_1_out2), .clk(clock_1_out), .Q(register_3_q));  // open: clr
  Register #(.width(32)) register_4 (.D(DATA), .en(decoder_1_out3), .clk(clock_1_out), .Q(register_4_q));  // open: clr
  Register #(.width(32)) register_5 (.D(DATA), .en(decoder_1_out4), .clk(clock_1_out), .Q(register_5_q));  // open: clr
  Register #(.width(32)) register_6 (.D(DATA), .en(decoder_1_out5), .clk(clock_1_out), .Q(register_6_q));  // open: clr
  Register #(.width(32)) register_7 (.D(DATA), .en(decoder_1_out6), .clk(clock_1_out), .Q(register_7_q));  // open: clr
  Register #(.width(32)) register_8 (.D(DATA), .en(decoder_1_out7), .clk(clock_1_out), .Q(register_8_q));  // open: clr
  Multiplexer #(.select(3), .width(32)) multiplexer_1 (
    .in0(register_1_q), .in1(register_2_q), .in2(register_3_q), .in3(register_4_q), .in4(register_5_q),
    .in5(register_6_q), .in6(register_7_q), .in7(register_8_q), .out(OUT1), .sel(RS1));
  Multiplexer #(.select(3), .width(32)) multiplexer_2 (
    .in0(register_1_q), .in1(register_2_q), .in2(register_3_q), .in3(register_4_q), .in4(register_5_q),
    .in5(register_6_q), .in6(register_7_q), .in7(register_8_q), .out(OUT2), .sel(RS2));
endmodule

module RegisterBank8Zero (
  input  [2:0] RS1,
  input  [2:0] RS2,
  input  [31:0] DATA,
  input  WRITE,
  input  [2:0] RD,
  output [31:0] OUT1,
  output [31:0] OUT2
);

  wire clock_1_out, decoder_1_out0, decoder_1_out1, decoder_1_out2, decoder_1_out3, decoder_1_out4,
       decoder_1_out5, decoder_1_out6, decoder_1_out7;
  wire [31:0] register_1_q, register_2_q, register_3_q, register_4_q, register_5_q, TEST1_q, TEST2_q, ZERO_q;

  Clock clock_1 (.out(clock_1_out));
  Decoder #(.select(3)) decoder_1 (
    .out0(decoder_1_out0), .out1(decoder_1_out1), .out2(decoder_1_out2), .out3(decoder_1_out3),
    .out4(decoder_1_out4), .out5(decoder_1_out5), .out6(decoder_1_out6), .out7(decoder_1_out7), .sel(RD),
    .en(WRITE));
  Register #(.width(32)) ZERO (.D({32{1'b0}}), .en(decoder_1_out0), .clk(clock_1_out), .Q(ZERO_q));  // open: clr
  Register #(.width(32)) TEST1 (.D(DATA), .en(decoder_1_out1), .clk(clock_1_out), .Q(TEST1_q));  // open: clr
  Register #(.width(32)) TEST2 (.D(DATA), .en(decoder_1_out2), .clk(clock_1_out), .Q(TEST2_q));  // open: clr
  Register #(.width(32)) register_1 (.D(DATA), .en(decoder_1_out3), .clk(clock_1_out), .Q(register_1_q));  // open: clr
  Register #(.width(32)) register_2 (.D(DATA), .en(decoder_1_out4), .clk(clock_1_out), .Q(register_2_q));  // open: clr
  Register #(.width(32)) register_3 (.D(DATA), .en(decoder_1_out5), .clk(clock_1_out), .Q(register_3_q));  // open: clr
  Register #(.width(32)) register_4 (.D(DATA), .en(decoder_1_out6), .clk(clock_1_out), .Q(register_4_q));  // open: clr
  Register #(.width(32)) register_5 (.D(DATA), .en(decoder_1_out7), .clk(clock_1_out), .Q(register_5_q));  // open: clr
  Multiplexer #(.select(3), .width(32)) multiplexer_1 (
    .in0(ZERO_q), .in1(TEST1_q), .in2(TEST2_q), .in3(register_1_q), .in4(register_2_q), .in5(register_3_q),
    .in6(register_4_q), .in7(register_5_q), .out(OUT1), .sel(RS1));
  Multiplexer #(.select(3), .width(32)) multiplexer_2 (
    .in0(ZERO_q), .in1(TEST1_q), .in2(TEST2_q), .in3(register_1_q), .in4(register_2_q), .in5(register_3_q),
    .in6(register_4_q), .in7(register_5_q), .out(OUT2), .sel(RS2));
endmodule
