// Logisim project SPC8.circ as structural Verilog: 5 circuits, main circuit main
module main (
);

  wire clock_1_out, conditions_1_jmp, instrdecoder_1_alu, instrdecoder_1_conditional, instrdecoder_1_read,
       instrdecoder_1_write;
  wire [1:0] instrdecoder_1_opcode;
  wire [2:0] instrdecoder_1_dest_reg, instrdecoder_1_src_reg;
  wire [3:0] instrdecoder_1_const;
  wire [7:0] counter_1_q, instrdecoder_1_jmp_adress, REGB_arg1, REGB_arg2, REGB_outputdata, rom_1_data;

  Clock clock_1 (.out(clock_1_out));
  Counter counter_1 (
    .load(conditions_1_jmp), .clk(clock_1_out), .D(instrdecoder_1_jmp_adress), .Q(counter_1_q));  // open: clr, up, count, carry
  ROM rom_1 (.addr(counter_1_q), .data(rom_1_data));
  // Probe on instrdecoder_1_dest_reg
  instrDecoder instrdecoder_1 (
    .INSTR(rom_1_data), .WRITE(instrdecoder_1_write), .READ(instrdecoder_1_read),
    .DEST_REG(instrdecoder_1_dest_reg), .SRC_REG(instrdecoder_1_src_reg), .OPCODE(instrdecoder_1_opcode),
    .ALU(instrdecoder_1_alu), .CONST(instrdecoder_1_const), .CONDITIONAL(instrdecoder_1_conditional),
    .JMP_ADRESS(instrdecoder_1_jmp_adress));
  RegisterBank REGB (
    .WriteReg(instrdecoder_1_dest_reg), .WRITE(instrdecoder_1_write), .READ(instrdecoder_1_read),
    .InputData(REGB_outputdata), .ReadReg(instrdecoder_1_src_reg), .OutputData(REGB_outputdata),
    .ARG1(REGB_arg1), .ARG2(REGB_arg2));
  // Probe on REGB_arg1
  // Probe on REGB_arg2
  Conditions conditions_1 (.ACTIVE(instrdecoder_1_conditional), .REG0(REGB_outputdata), .JMP(conditions_1_jmp));
  // Probe on REGB_outputdata
  ALU8V1 alu8v1_1 (
    .ARG2(REGB_arg2), .ARG1(REGB_arg1), .OPCODE(instrdecoder_1_opcode), .ACTIVE(instrdecoder_1_alu),
    .CONST(instrdecoder_1_const), .RESULT(REGB_outputdata));

  // Notes on the sheet:
  //   contents of rom_1 (hex, n*v repeats v):
  //   0 10 4d f0 2d 4 2d d 12
endmodule

module ALU8V1 (
  input  [7:0] ARG2,
  input  [7:0] ARG1,
  input  [1:0] OPCODE,
  input  ACTIVE,
  input  [3:0] CONST,
  output [7:0] RESULT
);

  wire decoder_1_out0, decoder_1_out1, decoder_1_out2, decoder_1_out3;
  wire [7:0] adder_1_out, adder_2_out, bit_extender_1_out, controlled_buffer_1_out, nand_1_out,
       subtractor_1_out;

  assign nand_1_out = ~(ARG1 & ARG2);  // NAND_Gate nand_1, 8 bits wide
  Subtractor subtractor_1 (.a(ARG1), .b(ARG2), .out(subtractor_1_out));  // open: bin, bout
  Adder adder_1 (.a(ARG1), .b(ARG2), .out(adder_1_out));  // open: cin, cout
  Decoder #(.disabled("Z"), .select(2)) decoder_1 (
    .out0(decoder_1_out0), .out1(decoder_1_out1), .out2(decoder_1_out2), .out3(decoder_1_out3), .sel(OPCODE),
    .en(ACTIVE));
  assign controlled_buffer_1_out = decoder_1_out2 ? nand_1_out : 8'bz;  // Controlled_Buffer controlled_buffer_1
  assign controlled_buffer_1_out = decoder_1_out1 ? subtractor_1_out : 8'bz;  // Controlled_Buffer controlled_buffer_2
  assign controlled_buffer_1_out = decoder_1_out0 ? adder_1_out : 8'bz;  // Controlled_Buffer controlled_buffer_3
  // Probe on decoder_1_out0
  assign bit_extender_1_out = {{4{1'b0}}, CONST};  // Bit_Extender bit_extender_1
  assign RESULT = ACTIVE ? adder_2_out : 8'bz;  // Controlled_Buffer controlled_buffer_4
  Adder adder_2 (.a(controlled_buffer_1_out), .b(bit_extender_1_out), .out(adder_2_out));  // open: cin, cout
endmodule

module RegisterBank (
  input  [2:0] WriteReg,
  input  WRITE,
  input  READ,
  input  [7:0] InputData,
  input  [2:0] ReadReg,
  output [7:0] OutputData,
  output [7:0] ARG1,
  output [7:0] ARG2
);

  wire clock_1_out, demultiplexer_1_out0, demultiplexer_1_out1, demultiplexer_1_out2, demultiplexer_1_out3,
       demultiplexer_1_out4, demultiplexer_1_out5, demultiplexer_1_out6, demultiplexer_1_out7;
  wire [7:0] REG0_q, REG3_q, REG4_q, REG5_q, REG6_q, REG7_q;

  Clock clock_1 (.out(clock_1_out));
  Demultiplexer #(.enable("true"), .select(3)) demultiplexer_1 (
    .out0(demultiplexer_1_out0), .out1(demultiplexer_1_out1), .out2(demultiplexer_1_out2),
    .out3(demultiplexer_1_out3), .out4(demultiplexer_1_out4), .out5(demultiplexer_1_out5),
    .out6(demultiplexer_1_out6), .out7(demultiplexer_1_out7), .in(1'b1), .sel(WriteReg), .en(WRITE));
  Pull_Resistor pull_resistor_1 (.node(READ));
  Register REG0 (.D(InputData), .en(demultiplexer_1_out0), .clk(clock_1_out), .Q(REG0_q));  // open: clr
  Register REG1 (.D(InputData), .en(demultiplexer_1_out1), .clk(clock_1_out), .Q(ARG1));  // open: clr
  Register REG2 (.D(InputData), .en(demultiplexer_1_out2), .clk(clock_1_out), .Q(ARG2));  // open: clr
  Register REG3 (.D(InputData), .en(demultiplexer_1_out3), .clk(clock_1_out), .Q(REG3_q));  // open: clr
  Register REG4 (.D(InputData), .en(demultiplexer_1_out4), .clk(clock_1_out), .Q(REG4_q));  // open: clr
  Register REG5 (.D(InputData), .en(demultiplexer_1_out5), .clk(clock_1_out), .Q(REG5_q));  // open: clr
  Register REG6 (.D(InputData), .en(demultiplexer_1_out6), .clk(clock_1_out), .Q(REG6_q));  // open: clr
  Register REG7 (.D(InputData), .en(demultiplexer_1_out7), .clk(clock_1_out), .Q(REG7_q));  // open: clr
  // Probe on READ
  Multiplexer #(.disabled("Z"), .enable("true"), .select(3), .width(8)) multiplexer_1 (
    .in0(REG0_q), .in1(ARG1), .in2(ARG2), .in3(REG3_q), .in4(REG4_q), .in5(REG5_q), .in6(REG6_q),
    .in7(REG7_q), .out(OutputData), .sel(ReadReg), .en(READ));
  // Probe on OutputData
endmodule

module instrDecoder (
  input  [7:0] INSTR,
  output WRITE,
  output READ,
  output [2:0] DEST_REG,
  output [2:0] SRC_REG,
  output [1:0] OPCODE,
  output ALU,
  output [3:0] CONST,
  output CONDITIONAL,
  output [7:0] JMP_ADRESS
);

  wire decoder_1_out1;

  // Probe on INSTR[1:0]
  Decoder #(.enable("false"), .select(2), .tristate("true")) decoder_1 (
    .out0(ALU), .out1(decoder_1_out1), .out2(CONDITIONAL), .sel(INSTR[1:0]));  // open: out3
  or or_1 (READ, decoder_1_out1, CONDITIONAL);
  or or_2 (WRITE, ALU, decoder_1_out1);
  Pull_Resistor pull_resistor_1 (.node(decoder_1_out1));
  Pull_Resistor pull_resistor_2 (.node(CONDITIONAL));
  Multiplexer #(.width(3)) multiplexer_1 (.in0(INSTR[7:5]), .in1(3'b011), .out(DEST_REG), .sel(ALU));
  // Probe on INSTR[4:2]
  Pull_Resistor pull_resistor_3 (.node(ALU));
  Multiplexer #(.width(3)) multiplexer_2 (.in0(INSTR[4:2]), .in1(3'b000), .out(SRC_REG), .sel(CONDITIONAL));
  assign JMP_ADRESS = {{2{1'b0}}, INSTR[7:2]};  // Bit_Extender bit_extender_1

  assign CONST = INSTR[7:4];
  assign OPCODE = INSTR[3:2];
endmodule

module Conditions (
  input  ACTIVE,
  input  [7:0] REG0,
  output JMP
);

  wire comparator_1_gt;

  Comparator comparator_1 (.a(REG0), .b({8{1'b0}}), .gt(comparator_1_gt));  // open: eq, lt
  assign JMP = ACTIVE ? comparator_1_gt : 1'bz;  // Controlled_Buffer controlled_buffer_1
endmodule
